# Fritzing sketch TodoJunto (saved by Fritzing 0.9.3b)
breadboards: 4

parts:
  Part1 = Arduino Mega 2560 (Rev3)
  LED1 = smd LED [color="Blue (430nm)" package="0603 [SMD]"]
  LED2 = smd LED [color="Blue (430nm)" package="0603 [SMD]"]
  LED3 = smd LED [color="Blue (430nm)" package="0603 [SMD]"]
  LED4 = smd LED [color="Blue (430nm)" package="0603 [SMD]"]
  LED5 = smd LED [color="Blue (430nm)" package="0603 [SMD]"]
  R1 = Resistor [tolerance=±5% resistance=220 package=THT]
  R2 = Resistor [tolerance=±5% resistance=220 package=THT]
  R3 = Resistor [tolerance=±5% resistance=220 package=THT]
  R4 = Resistor [tolerance=±5% resistance=220 package=THT]
  R5 = Resistor [tolerance=±5% resistance=220 package=THT]
  R6 = Resistor [tolerance=±5% resistance=220 package=THT]
  R7 = Resistor [tolerance=±5% resistance=220 package=THT]
  R8 = Resistor [tolerance=±5% resistance=220 package=THT]
  R9 = Resistor [tolerance=±5% resistance=220 package=THT]
  R10 = Resistor [tolerance=±5% resistance=220 package=THT]
  LED6 = smd LED [color="Red (633nm)" package="0603 [SMD]"]
  LED7 = smd LED [color="Red (633nm)" package="0603 [SMD]"]
  LED8 = smd LED [color="Red (633nm)" package="0603 [SMD]"]
  LED9 = smd LED [color="Red (633nm)" package="0603 [SMD]"]
  LED10 = smd LED [color="Red (633nm)" package="0603 [SMD]"]
  Componente1 = Bluetooth Mate Silver
  R11 = Resistor [tolerance=±5% resistance=220 package=THT]
  R12 = Resistor [tolerance=±5% resistance=220 package=THT]
  hc-sr1 = hc-sr04
  J1 = Piezo Speaker
  LED11 = LED - 5mm [color="Red (633nm)" package="5 mm [THT]"]
  U1 = MLX90614 [package=to-39]  # not connected
  LED12 = LED - 5mm [color="Red (633nm)" package="5 mm [THT]"]

nets:
  N1: Part1.D19/RX1, Componente1.VCC
  N2: Part1.D18/TX1, R12.Pin_1
  N3: Part1.D13_PWM, R10.Pin_0
  N4: Part1.D12_PWM, R8.Pin_0
  N5: Part1.D11_PWM, R9.Pin_0
  N6: Part1.D10_PWM, R7.Pin_0
  N7: Part1.D9_PWM, R6.Pin_0
  5V: Part1.5V, Componente1.RX_5V, hc-sr1.VCC
  GND: Part1.GND, LED1.anode, LED2.anode, LED3.anode, LED4.anode, LED5.anode, LED6.anode, LED7.anode, LED8.anode, LED9.anode, LED10.anode, Componente1.TX_5V, R11.Pin_0, hc-sr1.GND, J1.pin1, LED11.cathode, LED12.cathode
  N8: Part1.D2_PWM, R2.Pin_0
  N9: Part1.D3_PWM, R4.Pin_0
  N10: Part1.D4_PWM, R3.Pin_0
  N11: Part1.D5_PWM, R5.Pin_0
  N12: Part1.D6_PWM, R1.Pin_0
  N13: Part1.D41, LED12.anode
  N14: Part1.D50, J1.pin2
  N15: Part1.D51, LED11.anode
  N16: Part1.D52, hc-sr1.Trig
  N17: Part1.D53, hc-sr1.Echo
  N18: LED1.cathode, R1.Pin_1
  N19: LED2.cathode, R3.Pin_1
  N20: LED3.cathode, R4.Pin_1
  N21: LED4.cathode, R2.Pin_1
  N22: LED5.cathode, R5.Pin_1
  N23: R6.Pin_1, LED7.cathode
  N24: R7.Pin_1, LED8.cathode
  N25: R8.Pin_1, LED6.cathode
  N26: R9.Pin_1, LED9.cathode
  N27: R10.Pin_1, LED10.cathode
  N28: Componente1.CTS_5V, R11.Pin_1, R12.Pin_0
