# Fritzing sketch luces del coche fantastico (saved by Fritzing 0.9.3b)
breadboards: 1

parts:
  Part2 = Arduino Mega 2560 (Rev3)
  R6 = Resistor [tolerance=±5% resistance=220 package=THT]
  R7 = Resistor [tolerance=±5% resistance=220 package=THT]
  R8 = Resistor [tolerance=±5% resistance=220 package=THT]
  R9 = Resistor [tolerance=±5% resistance=220 package=THT]
  R10 = Resistor [tolerance=±5% resistance=220 package=THT]
  LED6 = smd LED [color="Red (633nm)" package="0603 [SMD]"]
  LED7 = smd LED [color="Red (633nm)" package="0603 [SMD]"]
  LED8 = smd LED [color="Red (633nm)" package="0603 [SMD]"]
  LED9 = smd LED [color="Red (633nm)" package="0603 [SMD]"]
  LED10 = smd LED [color="Red (633nm)" package="0603 [SMD]"]

nets:
  N1: Part2.GND, LED6.anode, LED7.anode, LED8.anode, LED9.anode, LED10.anode
  N2: Part2.D2_PWM, R6.Pin_0
  N3: Part2.D3_PWM, R7.Pin_0
  N4: Part2.D4_PWM, R9.Pin_0
  N5: Part2.D5_PWM, R8.Pin_0
  N6: Part2.D6_PWM, R10.Pin_0
  N7: R6.Pin_1, LED7.cathode
  N8: R7.Pin_1, LED8.cathode
  N9: R8.Pin_1, LED6.cathode
  N10: R9.Pin_1, LED9.cathode
  N11: R10.Pin_1, LED10.cathode
