# Fritzing sketch sensor de movimiento PIR (saved by Fritzing 0.9.3b)
breadboards: 1

parts:
  Part2 = Arduino Mega 2560 (Rev3)
  U2 = MLX90614 [package=to-39]  # not connected
  LED1 = LED - 5mm [color="Red (633nm)" package="5 mm [THT]"]

nets:
  N1: Part2.GND, LED1.cathode
  N2: Part2.D41, LED1.anode
