# Fritzing sketch sensor de ultrasonido (saved by Fritzing 0.9.3b)
breadboards: 1

parts:
  Part2 = Arduino Mega 2560 (Rev3)
  hc-sr2 = hc-sr04
  J2 = Piezo Speaker
  LED12 = LED - 5mm [color="Red (633nm)" package="5 mm [THT]"]

nets:
  5V: Part2.5V, hc-sr2.VCC
  N1: Part2.D50, J2.pin2
  N2: Part2.D51, LED12.anode
  N3: Part2.D52, hc-sr2.Trig
  N4: Part2.D53, hc-sr2.Echo
  N5: hc-sr2.GND, LED12.cathode
